// Logisim project cpu.circ as structural Verilog: 1 circuit, main circuit main
module main (
  output [15:0] PC,
  output [7:0] A,
  output halt,
  output [15:0] insn,
  output [7:0] B
);

  wire clock_1_out, clock_2_out, clock_3_out, clock_4_out, not_1_out, ROM_sel, undriven, undriven_2;
  wire [7:0] memdata, multiplexer_3_out;
  wire [15:0] adder_1_out, bit_extender_1_out, multiplexer_1_out;

  // Probe on PC
  // Probe on insn[7:0]
  // Probe on insn[15:8]
  Multiplexer #(.width(16)) multiplexer_1 (
    .in0(16'h1), .in1(bit_extender_1_out), .out(multiplexer_1_out), .sel(insn[0]), .en(1'b1));
  assign bit_extender_1_out = {{8{insn[15]}}, insn[15:8]};  // Bit_Extender bit_extender_1
  // Probe on insn[15:8]
  // Probe on memdata
  Adder #(.width(16)) adder_1 (.a(PC), .b(multiplexer_1_out), .out(adder_1_out));  // open: cin, cout
  // Probe on A
  // Probe on B
  Register #(.width(16)) u_PC (.D(adder_1_out), .Q(PC), .clk(clock_1_out));  // open: en, clr
  Clock clock_1 (.out(clock_1_out));
  rom ROM (.A(PC), .sel(ROM_sel), .D(insn));
  // Probe on insn
  Comparator #(.width(16), .mode("unsigned")) comparator_1 (.a(insn), .b(16'h1), .eq(halt));  // open: gt, lt
  Clock clock_2 (.out(clock_2_out));
  not not_1 (not_1_out, insn[1]);
  Multiplexer #(.width(8)) multiplexer_2 (.in0(A), .in1(B), .out(memdata), .sel(insn[5]), .en(insn[1]));
  RAM #(.bus("asynch")) ram_1 (.addr(insn[15:8]), .data(memdata), .sel(1'b1), .ld(not_1_out));  // open: clr
  Multiplexer #(.width(8)) multiplexer_3 (
    .in0(memdata), .in1(insn[15:8]), .out(multiplexer_3_out), .sel(insn[4]));  // open: en
  Register register_1 (.D(multiplexer_3_out), .en(insn[2]), .Q(A), .clk(clock_3_out), .clr(undriven));
  Clock clock_3 (.out(clock_3_out));
  Register register_2 (.D(multiplexer_3_out), .en(insn[3]), .Q(B), .clk(clock_4_out), .clr(undriven_2));
  Clock clock_4 (.out(clock_4_out));
  // also tied to VCC on the sheet: ROM_sel

  // Other names for the same wires on the sheet: ctl[7:0] = insn[7:0]; ctl_jmp = insn[0]; ctl_mwr = insn[1];
  //   ctl_wra = insn[2]; ctl_wrb = insn[3]; ctl_ldmem_ldimm = insn[4]; ctl_sta_stb = insn[5]; imm[7:0] = insn[15:8];
  //   memaddr[7:0] = insn[15:8]
endmodule
